# Fritzing sketch horloge_arduino (saved by Fritzing 0.9.3b)
breadboards: 1

parts:
  Composant1 = Arduino Uno (Rev3)
  U3 = POT [package=alps_pot]
  IR1 = TSOP312.., 314.. [package=THT]
  ZS-042_RTC1 = ZS-042 RTC Module
  LCD2 = LCD screen

nets:
  N1: Composant1.A4/SDA, ZS-042_RTC1.SDA
  N2: Composant1.A5/SCL, ZS-042_RTC1.SCL
  N3: Composant1.D1/TX, LCD2.RS
  N4: Composant1.D2, LCD2.E
  N5: Composant1.D3_PWM, IR1.GND
  N6: Composant1.D4, LCD2.DB4
  N7: Composant1.D5_PWM, LCD2.DB5
  N8: Composant1.D6_PWM, LCD2.DB6
  N9: Composant1.D7, LCD2.DB7
  5V: Composant1.5V, U3.A, IR1.Data, ZS-042_RTC1.VCC, LCD2.VDD, LCD2.LED+
  GND: Composant1.GND, U3.E, IR1.Vs, ZS-042_RTC1.GND, LCD2.VSS, LCD2.R/W, LCD2.LED-
  N10: U3.S, LCD2.V0
